// Logisim project Project3Given.circ as structural Verilog: 14 circuits, main circuit CPU15
module main (
  input  EnableBreakpoint,
  input  [14:0] Breakpoint
);

  wire and_2_out, and_3_out, chipset_1_irq, CLK, clock_1_out, cpu15_1_c, cpu15_1_e, cpu15_1_i, cpu15_1_n,
       cpu15_1_o, cpu15_1_z, KBCLR, KBIRQ, KBRD, MEMCS, nand_1_out, RE, TTYCLR, TTYWE, WE;
  wire [6:0] KBDATA, TTYDATA;
  wire [7:0] cpu15_1_srf;
  wire [14:0] ADDR, chipset_1_ivect, chipset_1_led0, chipset_1_led1, chipset_1_led2, chipset_1_led3,
       chipset_1_led4, chipset_1_led5, chipset_1_led6, chipset_1_led7, chipset_1_led8, chipset_1_led9,
       chipset_1_leda, chipset_1_ledb, chipset_1_ledc, chipset_1_ledd, chipset_1_lede, cpu15_1_ib,
       cpu15_1_pc, cpu15_1_r0, cpu15_1_r1, cpu15_1_r2, cpu15_1_r3, cpu15_1_r4, cpu15_1_r5, cpu15_1_r6,
       cpu15_1_r7, cpu15_1_srp, DATA, xnor_1_out;

  Clock clock_1 (.out(clock_1_out));
  nand nand_1 (nand_1_out, EnableBreakpoint, xnor_1_out[0], xnor_1_out[1], xnor_1_out[2], xnor_1_out[3], xnor_1_out[4], xnor_1_out[5], xnor_1_out[6], xnor_1_out[7], xnor_1_out[8], xnor_1_out[9], xnor_1_out[10], xnor_1_out[11], xnor_1_out[12], xnor_1_out[13], xnor_1_out[14], 1'b1);
  and and_1 (CLK, clock_1_out, nand_1_out);
  assign xnor_1_out = ~(Breakpoint ^ cpu15_1_pc);  // XNOR_Gate xnor_1, 15 bits wide
  LED I (.in(cpu15_1_i));
  LED Z (.in(cpu15_1_z));
  LED N (.in(cpu15_1_n));
  LED O (.in(cpu15_1_o));
  LED C (.in(cpu15_1_c));
  LED E (.in(cpu15_1_e));
  and and_2 (and_2_out, WE, MEMCS);
  and and_3 (and_3_out, MEMCS, RE);
  RAM #(.addrWidth(15), .dataWidth(15)) ram_1 (.addr(ADDR), .we(and_2_out), .oe(and_3_out), .clk(CLK), .data(DATA));
  // Probe on cpu15_1_pc
  // Probe on cpu15_1_ib
  // Probe on cpu15_1_srp
  // Probe on cpu15_1_srf
  // Probe on cpu15_1_r0
  // Probe on cpu15_1_r1
  // Probe on cpu15_1_r2
  // Probe on cpu15_1_r3
  // Probe on cpu15_1_r4
  // Probe on cpu15_1_r5
  // Probe on cpu15_1_r6
  // Probe on cpu15_1_r7
  CPU15 cpu15_1 (
    .I(cpu15_1_i), .Z(cpu15_1_z), .N(cpu15_1_n), .O(cpu15_1_o), .C(cpu15_1_c), .E(cpu15_1_e),
    .PC(cpu15_1_pc), .IB(cpu15_1_ib), .SRP(cpu15_1_srp), .SRF(cpu15_1_srf), .R0(cpu15_1_r0), .R1(cpu15_1_r1),
    .R2(cpu15_1_r2), .R3(cpu15_1_r3), .R4(cpu15_1_r4), .R5(cpu15_1_r5), .R6(cpu15_1_r6), .R7(cpu15_1_r7),
    .CLK(CLK), .IRQ(chipset_1_irq), .RE(RE), .WE(WE), .ADDR(ADDR), .DATAIN(DATA), .DATAOUT(DATA));
  // Probe on ADDR
  // Probe on DATA
  // Probe on chipset_1_ivect
  // Probe on TTYDATA
  CHIPSET chipset_1 (
    .RE(RE), .WE(WE), .ADDR(ADDR), .CPUDATAIN(DATA), .CPUDATAOUT(DATA), .IRQ(chipset_1_irq),
    .IVECT(chipset_1_ivect), .CLK(CLK), .MEMCS(MEMCS), .TTYWR(TTYWE), .TTYCLR(TTYCLR), .TTYDATA(TTYDATA),
    .KBRD(KBRD), .KBCLR(KBCLR), .KBIRQ(KBIRQ), .KBDATA(KBDATA), .LED0(chipset_1_led0), .LED1(chipset_1_led1),
    .LED2(chipset_1_led2), .LED3(chipset_1_led3), .LED4(chipset_1_led4), .LED5(chipset_1_led5),
    .LED6(chipset_1_led6), .LED7(chipset_1_led7), .LED8(chipset_1_led8), .LED9(chipset_1_led9),
    .LEDA(chipset_1_leda), .LEDB(chipset_1_ledb), .LEDC(chipset_1_ledc), .LEDD(chipset_1_ledd),
    .LEDE(chipset_1_lede));
  TTY tty_1 (.data(TTYDATA), .clk(CLK), .we(TTYWE), .clr(TTYCLR));
  Keyboard keyboard_1 (.clk(CLK), .re(KBRD), .clr(KBCLR), .avail(KBIRQ), .data(KBDATA));
  DotMatrix #(.matrixcols(15), .matrixrows(15)) dotmatrix_1 (
    .col0(chipset_1_led0), .col1(chipset_1_led1), .col2(chipset_1_led2), .col3(chipset_1_led3),
    .col4(chipset_1_led4), .col5(chipset_1_led5), .col6(chipset_1_led6), .col7(chipset_1_led7),
    .col8(chipset_1_led8), .col9(chipset_1_led9), .col10(chipset_1_leda), .col11(chipset_1_ledb),
    .col12(chipset_1_ledc), .col13(chipset_1_ledd), .col14(chipset_1_lede));
  // Probe on DATA[14:11]
  // Probe on DATA[10:8]
  // Probe on KBDATA
  // Probe on DATA[4:0]
  // Probe on DATA[7:5]
endmodule

// CPU
module CPU15 (
  input  [14:0] DATAIN,
  input  CLK,
  input  IRQ,
  output [14:0] PC,
  output [14:0] IB,
  output [14:0] SRP,
  output [7:0] SRF,
  output [14:0] R0,
  output [14:0] R1,
  output [14:0] R2,
  output [14:0] R3,
  output [14:0] R4,
  output [14:0] R5,
  output [14:0] R6,
  output [14:0] R7,
  output RE,
  output WE,
  output I,
  output Z,
  output [14:0] ADDR,
  output N,
  output O,
  output C,
  output E,
  output [14:0] DATAOUT
);

  wire a1, ALu_t, alU_t_t, ALuf, and_2_out, and_3_out, and_4_out, and_5_out, and_8_out, count,
       counter_1_carry, dataTopc, decoder_2_out3, decoder_6_out2, exdataTopc, exload, forward, imm10,
       interrupt, jump, jumpin, KLC, load, multiplexer_2_out, multiplexer_3_out, not_2_out, not_3_out,
       not_5_out, not_6_out, not_7_out, not_8_out, not_9_out, not_10_out, not_11_out, not_12_out, or_1_out,
       or_2_out, or_4_out, or_6_out, or_7_out, or_8_out, or_9_out, or_10_out, preload, RE_t, regW, REing,
       SRf_t, SRFW, sRP_t, SRPW, stLOAD, stSTORE, SWI, tALU, tF, tird, tisr, tisr2, tisrlift, tPC, tsr1,
       tsr2, tSRF, tSRP, tzero, undriven;
  wire [0:0] decode15_1_aluop;
  wire [1:0] decode15_1_asel, decode15_1_bsel, decode15_1_flagsrc, decode15_1_pwsrc;
  wire [2:0] ALUOP, controlled_buffer_31_out, decode15_1_regdatasrc, register_8_q;
  wire [3:0] alu15_1_z;
  wire [7:0] ALUFLAG, controlled_buffer_25_out, flagWm;
  wire [7:4] F;
  wire [14:0] ALU, bit_extender_2_out, bit_extender_3_out, bit_extender_4_out, bit_extender_5_out,
       bit_extender_7_out, bit_extender_8_out, controlled_buffer_2_out, controlled_buffer_6_out,
       controlled_buffer_7_out, controlled_buffer_10_out, controlled_buffer_14_out, controlled_buffer_17_out,
       controlled_buffer_19_out, controlled_buffer_28_out, controlled_buffer_30_out,
       controlled_buffer_32_out, controlled_buffer_40_out, DATA, DATAOUT_t, isr2, jumpto, NPC, register_1_q,
       register_3_q, register_5_q, register_9_q, sDATA, sr1, sr2;

  not not_1 (KLC, CLK);
  D_Flip_Flop d_ff_1 (.clk(stSTORE), .D(1'b0), .preset(WE));  // open: Q, Qn, reset
  Multiplexer #(.enable("false")) multiplexer_1 (.in0(stSTORE), .in1(1'b0), .sel(WE));  // open: out
  D_Flip_Flop d_ff_2 (.D(stLOAD), .clk(KLC), .Q(preload));  // open: Qn, preset, reset
  D_Flip_Flop d_ff_3 (.D(preload), .clk(CLK), .Q(exload));  // open: Qn, preset, reset
  Register #(.width(15)) register_1 (.D(ALU), .clk(KLC), .Q(register_1_q));  // open: en, clr
  Register #(.width(15)) register_2 (.D(DATA), .en(forward), .clk(CLK), .Q(IB), .clr(or_1_out));
  assign DATAOUT_t = WE ? sr2 : 15'bz;  // Controlled_Buffer controlled_buffer_1
  or or_1 (or_1_out, jumpin, REing);
  and and_1 (load, stLOAD, exload);
  D_Flip_Flop d_ff_4 (.D(load), .clk(KLC), .Q(REing));  // open: Qn, preset, reset
  assign controlled_buffer_2_out = not_2_out ? NPC : 15'bz;  // Controlled_Buffer controlled_buffer_2
  not not_2 (not_2_out, or_2_out);
  assign controlled_buffer_2_out = or_2_out ? register_1_q : 15'bz;  // Controlled_Buffer controlled_buffer_3
  or or_2 (or_2_out, WE, preload);
  or or_3 (RE, REing, and_2_out);
  and and_2 (and_2_out, RE_t, CLK);
  assign sDATA = RE_t ? DATAIN : 15'bz;  // Controlled_Buffer controlled_buffer_4
  assign DATAOUT = WE ? DATAOUT_t : 15'bz;  // Controlled_Buffer controlled_buffer_5
  // Probe on IB[14]
  // Probe on IB[13:11]
  Register #(.width(15)) register_3 (.D(jumpto), .clk(KLC), .Q(register_3_q));  // open: en, clr
  // Probe on ADDR
  // Probe on DATAIN
  assign controlled_buffer_6_out = RE_t ? sDATA : 15'bz;  // Controlled_Buffer controlled_buffer_6
  and and_3 (and_3_out, ~exload, stSTORE);  // AND_Gate
  assign isr2 = {{11{IB[14]}}, IB[14:11]};  // Bit_Extender bit_extender_1
  // Probe on IB[7:5]
  // Probe on IB[10:8]
  assign controlled_buffer_7_out = not_3_out ? controlled_buffer_2_out : 15'bz;  // Controlled_Buffer controlled_buffer_7
  not not_3 (not_3_out, jump);
  not not_4 (RE_t, WE);
  Register #(.width(15)) register_4 (.D(controlled_buffer_6_out), .clk(KLC), .Q(DATA));  // open: en, clr
  assign controlled_buffer_6_out = WE ? {15{1'b0}} : 15'bz;  // Controlled_Buffer controlled_buffer_8
  nor nor_1 (forward, jumpin, exload, preload, WE, exdataTopc);
  nor nor_2 (count, stLOAD, preload, and_3_out);
  // Probe on IB[14:8]
  // Probe on IB[4:0]
  assign controlled_buffer_7_out = jump ? register_3_q : 15'bz;  // Controlled_Buffer controlled_buffer_9
  // Probe on R2
  assign bit_extender_2_out = {{5{IB[14]}}, IB[14:5]};  // Bit_Extender bit_extender_2
  assign bit_extender_3_out = {{4{IB[14]}}, {IB[14:8], 4'b0000}};  // Bit_Extender bit_extender_3
  assign bit_extender_4_out = {{8{IB[14]}}, IB[14:8]};  // Bit_Extender bit_extender_4
  assign controlled_buffer_10_out = tsr2 ? sr2 : 15'bz;  // Controlled_Buffer controlled_buffer_10
  assign controlled_buffer_10_out = tisr2 ? isr2 : 15'bz;  // Controlled_Buffer controlled_buffer_11
  assign controlled_buffer_10_out = tzero ? R0 : 15'bz;  // Controlled_Buffer controlled_buffer_12
  assign bit_extender_5_out = {{12{1'b0}}, IB[7:5]};  // Bit_Extender bit_extender_5
  assign controlled_buffer_10_out = tird ? bit_extender_5_out : 15'bz;  // Controlled_Buffer controlled_buffer_13
  Register #(.width(15)) register_5 (.D(register_1_q), .clk(CLK), .Q(register_5_q));  // open: en, clr
  // Probe on R3
  assign controlled_buffer_14_out = SRPW ? ALU : 15'bz;  // Controlled_Buffer controlled_buffer_14
  assign controlled_buffer_14_out = SWI ? NPC : 15'bz;  // Controlled_Buffer controlled_buffer_15
  assign controlled_buffer_14_out = interrupt ? PC : 15'bz;  // Controlled_Buffer controlled_buffer_16
  Register #(.width(15)) register_6 (.D(controlled_buffer_14_out), .en(or_4_out), .clk(KLC), .Q(SRP));  // open: clr
  or or_4 (or_4_out, interrupt, SWI, SRPW);
  assign controlled_buffer_17_out = not_5_out ? controlled_buffer_7_out : 15'bz;  // Controlled_Buffer controlled_buffer_17
  not not_5 (not_5_out, REing);
  assign controlled_buffer_17_out = REing ? register_5_q : 15'bz;  // Controlled_Buffer controlled_buffer_18
  assign controlled_buffer_19_out = tsr1 ? sr1 : 15'bz;  // Controlled_Buffer controlled_buffer_19
  assign controlled_buffer_19_out = imm10 ? bit_extender_2_out : 15'bz;  // Controlled_Buffer controlled_buffer_20
  assign controlled_buffer_19_out = tisrlift ? bit_extender_3_out : 15'bz;  // Controlled_Buffer controlled_buffer_21
  assign controlled_buffer_19_out = tisr ? bit_extender_4_out : 15'bz;  // Controlled_Buffer controlled_buffer_22
  DECODE15 decode15_1 (
    .SWI(SWI), .FLAGWM(flagWm), .ALUOP({ALUOP[2:1], decode15_1_aluop[0]}), .BSEL(decode15_1_bsel),
    .SRFW(SRFW), .STORE(stSTORE), .FLAGSRC(decode15_1_flagsrc), .SRPW(SRPW), .REGW(regW), .OPCODE(IB[4:0]),
    .REGDATASRC(decode15_1_regdatasrc), .ASEL(decode15_1_asel), .LOAD(stLOAD), .PWSRC(decode15_1_pwsrc));
  assign ADDR = not_6_out ? controlled_buffer_17_out : 15'bz;  // Controlled_Buffer controlled_buffer_23
  not not_6 (not_6_out, dataTopc);
  Register register_7 (.D(ALU[7:0]), .en(SRFW), .clk(CLK), .Q(SRF));  // open: clr
  Decoder #(.select(2)) decoder_1 (
    .out0(tsr2), .out1(tisr2), .out2(tzero), .out3(tird), .sel(decode15_1_bsel));  // open: en
  Decoder #(.select(2)) decoder_2 (
    .out0(a1), .out1(alU_t_t), .out2(sRP_t), .out3(decoder_2_out3), .sel(decode15_1_pwsrc), .en(undriven));
  Decoder #(.select(2)) decoder_3 (
    .out0(a1), .out1(alU_t_t), .out2(sRP_t), .out3(decoder_2_out3), .sel(decode15_1_pwsrc), .en(undriven));
  assign ADDR = dataTopc ? {15{1'b1}} : 15'bz;  // Controlled_Buffer controlled_buffer_24
  // Probe on R6
  and and_4 (and_4_out, stSTORE, IB[14]);
  or or_5 (ALUOP[0], and_4_out, decode15_1_aluop[0]);
  not not_7 (not_7_out, Z);
  not not_8 (not_8_out, N);
  not not_9 (not_9_out, C);
  // Probe on R7
  assign controlled_buffer_25_out = ALu_t ? ALU[7:0] : 8'bz;  // Controlled_Buffer controlled_buffer_25
  assign controlled_buffer_25_out = ALuf ? ALUFLAG : 8'bz;  // Controlled_Buffer controlled_buffer_26
  assign controlled_buffer_25_out = SRf_t ? SRF : 8'bz;  // Controlled_Buffer controlled_buffer_27
  Decoder #(.select(2)) decoder_4 (
    .out0(tsr1), .out1(imm10), .out2(tisrlift), .out3(tisr), .sel(decode15_1_asel));  // open: en
  Decoder #(.select(3)) decoder_5 (
    .out0(tALU), .out1(tSRP), .out2(tSRF), .out3(tPC), .out4(tF), .sel(decode15_1_regdatasrc));  // open: out5, out6, out7, en
  Decoder #(.select(2)) decoder_6 (
    .out0(ALuf), .out1(ALu_t), .out2(decoder_6_out2), .out3(SRf_t), .sel(decode15_1_flagsrc));  // open: en
  Multiplexer #(.select(3), .enable("false")) multiplexer_2 (
    .in0(Z), .in1(not_7_out), .in2(N), .in3(not_8_out), .in4(C), .in5(not_9_out), .in6(1'b0), .in7(1'b0),
    .out(multiplexer_2_out), .sel(IB[2:0]));
  FLAGS8 flags8_1 (
    .F({F[7], I, E, F[4], O, C, N, Z}), .CLK(KLC), .WM(flagWm), .IRQ(IRQ), .NF(controlled_buffer_25_out));
  // Probe on controlled_buffer_25_out
  // Probe on ALUOP
  // Probe on controlled_buffer_10_out
  ALU15 alu15_1 (
    .C(alu15_1_z[2]), .R_2(ALU), .N(alu15_1_z[1]), .B(controlled_buffer_10_out),
    .A(controlled_buffer_19_out), .Z(alu15_1_z[0]), .OP(ALUOP), .O(alu15_1_z[3]));  // open: OIN, CIN, R
  // Probe on ALU
  // Probe on controlled_buffer_19_out
  // Probe on ALUFLAG
  Bit_Extender #(.in_width(4), .out_width(8), .\type ("input")) bit_extender_6 (
    .in(alu15_1_z), .out(ALUFLAG));  // open: extend
  or or_6 (or_6_out, multiplexer_2_out, IB[3]);
  // Probe on flagWm
  and and_5 (and_5_out, decoder_2_out3, or_6_out);
  assign bit_extender_7_out = {{7{1'b0}}, SRF};  // Bit_Extender bit_extender_7
  assign bit_extender_8_out = {{7{1'b0}}, {F[7], I, E, F[4], O, C, N, Z}};  // Bit_Extender bit_extender_8
  Register #(.width(3)) register_8 (.D(IB[7:5]), .clk(KLC), .Q(register_8_q));  // open: en, clr
  // Probe on ALU
  ADDER15 adder15_1 (.B(ALU), .A(PC), .S(jumpto));  // open: COUT, CIN
  // Probe on PC
  // Probe on jumpto
  and and_6 (jump, or_7_out, ~alU_t_t);  // AND_Gate
  or or_7 (or_7_out, alU_t_t, interrupt, and_5_out);
  not not_10 (not_10_out, load);
  assign controlled_buffer_28_out = tPC ? NPC : 15'bz;  // Controlled_Buffer controlled_buffer_28
  assign controlled_buffer_28_out = tF ? bit_extender_8_out : 15'bz;  // Controlled_Buffer controlled_buffer_29
  assign controlled_buffer_30_out = load ? sDATA : 15'bz;  // Controlled_Buffer controlled_buffer_30
  assign controlled_buffer_31_out = load ? register_8_q : 3'bz;  // Controlled_Buffer controlled_buffer_31
  assign controlled_buffer_32_out = alU_t_t ? ALU : 15'bz;  // Controlled_Buffer controlled_buffer_32
  D_Flip_Flop d_ff_5 (.D(multiplexer_3_out), .clk(KLC), .Q(jumpin));  // open: Qn, preset, reset
  Multiplexer #(.enable("false")) multiplexer_3 (.in0(or_7_out), .in1(1'b0), .out(multiplexer_3_out), .sel(jumpin));
  assign controlled_buffer_28_out = tALU ? ALU : 15'bz;  // Controlled_Buffer controlled_buffer_33
  assign controlled_buffer_30_out = not_10_out ? controlled_buffer_28_out : 15'bz;  // Controlled_Buffer controlled_buffer_34
  assign controlled_buffer_28_out = tSRP ? SRP : 15'bz;  // Controlled_Buffer controlled_buffer_35
  assign controlled_buffer_28_out = tSRF ? bit_extender_7_out : 15'bz;  // Controlled_Buffer controlled_buffer_36
  assign controlled_buffer_31_out = not_10_out ? IB[7:5] : 3'bz;  // Controlled_Buffer controlled_buffer_37
  not not_11 (not_11_out, dataTopc);
  assign controlled_buffer_32_out = jump ? jumpto : 15'bz;  // Controlled_Buffer controlled_buffer_38
  assign controlled_buffer_32_out = sRP_t ? SRP : 15'bz;  // Controlled_Buffer controlled_buffer_39
  or or_8 (or_8_out, load, regW);
  Counter #(.width(15), .max('h7fff)) counter_1 (
    .load(or_9_out), .up(1'b1), .count(and_8_out), .clk(KLC), .D(controlled_buffer_40_out),
    .carry(counter_1_carry), .Q(NPC));  // open: clr
  or or_9 (or_9_out, jump, dataTopc, sRP_t, alU_t_t);
  assign controlled_buffer_40_out = not_11_out ? controlled_buffer_32_out : 15'bz;  // Controlled_Buffer controlled_buffer_40
  assign controlled_buffer_40_out = dataTopc ? sDATA : 15'bz;  // Controlled_Buffer controlled_buffer_41
  or or_10 (or_10_out, interrupt, SWI);
  // Probe on IB[7:5]
  and and_7 (interrupt, IRQ, E);
  D_Flip_Flop d_ff_6 (.D(or_10_out), .clk(KLC), .Q(dataTopc));  // open: Qn, preset, reset
  and and_8 (and_8_out, not_12_out, count);
  D_Flip_Flop d_ff_7 (.D(dataTopc), .clk(KLC), .Q(exdataTopc));  // open: Qn, preset, reset
  // Probe on sr1
  REGS15 regs15_1 (
    .R4(R4), .A(sr1), .SelD(controlled_buffer_31_out), .R0(R0), .CLK(KLC), .B(sr2), .R5(R5), .R1(R1),
    .R3(R3), .R7(R7), .W(or_8_out), .SelB(IB[13:11]), .SelA(IB[10:8]), .D(controlled_buffer_30_out), .R6(R6),
    .R2(R2));
  // Probe on sr2
  not not_12 (not_12_out, counter_1_carry);
  Register #(.width(15)) register_9 (.D(NPC), .clk(KLC), .Q(register_9_q));  // open: en, clr
  Register #(.width(15)) register_10 (.D(register_9_q), .clk(CLK), .Q(PC));  // open: en, clr

  // Other names for the same wires on the sheet: arg[9:0] = IB[14:5]; ssr1[2:0] = IB[10:8]; ssr2[2:0] = IB[13:11];
  //   SSign = IB[14]; F (some bits) = {I, E, O, C, N, Z}; OP[3:0] = IB[3:0]; srd[2:0] = IB[7:5]; zero[14:0] = R0
endmodule

module CHIPSET (
  input  RE,
  input  WE,
  input  [14:0] ADDR,
  input  [14:0] CPUDATAIN,
  input  KBIRQ,
  input  [6:0] KBDATA,
  input  CLK,
  output MEMCS,
  output TTYWR,
  output [14:0] IVECT,
  output TTYCLR,
  output [6:0] TTYDATA,
  output KBRD,
  output KBCLR,
  output [14:0] CPUDATAOUT,
  output IRQ,
  output [14:0] LED0,
  output [14:0] LED1,
  output [14:0] LED2,
  output [14:0] LED3,
  output [14:0] LED4,
  output [14:0] LED5,
  output [14:0] LED6,
  output [14:0] LED7,
  output [14:0] LED8,
  output [14:0] LED9,
  output [14:0] LEDA,
  output [14:0] LEDB,
  output [14:0] LEDC,
  output [14:0] LEDD,
  output [14:0] LEDE
);

  wire and_1_out, and_8_out, and_10_out, controlled_buffer_4_out, d_ff_3_q, DATA7, IOCS, IVECTADDR, IVECTEN,
       IVECTRE, KBCS, LED0EN, LED0END, LED1EN, LED1END, LED2EN, LED2END, LED3EN, LED3END, LED4EN, LED4END,
       LED5EN, LED5END, LED6EN, LED6END, LED7EN, LED7END, LED8EN, LED8END, LED9EN, LED9END, LEDAEN, LEDAEND,
       LEDBEN, LEDBEND, LEDCEN, LEDCEND, LEDCS, LEDDEN, LEDDEND, LEDEEN, LEDEEND, LEDFEND, LEDRE,
       multiplexer_17_out, multiplexer_18_out, multiplexer_19_out, RWE, TTYCS, undriven;
  wire [14:0] DATAL0, DATAL1, DATAL2, DATAL3, DATAL4, DATAL5, DATAL6, DATAL7, DATAL8, DATAL9, DATALA, DATALB,
       DATALC, DATALD, DATALE, LEDDATA;
  wire [14:8] KBDATA15;

  Register #(.width(15)) register_1 (.D(DATAL0), .en(LED0EN), .clk(CLK), .Q(LED0));  // open: clr
  Register #(.width(15)) register_2 (.D(DATAL1), .en(LED1EN), .clk(CLK), .Q(LED1));  // open: clr
  Register #(.width(15)) register_3 (.D(DATAL2), .en(LED2EN), .clk(CLK), .Q(LED2));  // open: clr
  Register #(.width(15)) register_4 (.D(DATAL3), .en(LED3EN), .clk(CLK), .Q(LED3));  // open: clr
  Register #(.width(15)) register_5 (.D(DATAL4), .en(LED4EN), .clk(CLK), .Q(LED4));  // open: clr
  assign CPUDATAOUT = KBRD ? {KBDATA15, DATA7, KBDATA} : 15'bz;  // Controlled_Buffer controlled_buffer_1
  assign CPUDATAOUT = LEDRE ? LEDDATA : 15'bz;  // Controlled_Buffer controlled_buffer_2
  assign CPUDATAOUT = IVECTRE ? IVECT : 15'bz;  // Controlled_Buffer controlled_buffer_3
  and and_1 (and_1_out, WE, LEDCS);
  Register #(.width(15)) register_6 (.D(DATAL5), .en(LED5EN), .clk(CLK), .Q(LED5));  // open: clr
  Register #(.width(15)) register_7 (.D(DATAL6), .en(LED6EN), .clk(CLK), .Q(LED6));  // open: clr
  Register #(.width(15)) register_8 (.D(DATAL7), .en(LED7EN), .clk(CLK), .Q(LED7));  // open: clr
  Register #(.width(15)) register_9 (.D(DATAL8), .en(LED8EN), .clk(CLK), .Q(LED8));  // open: clr
  Register #(.width(15)) register_10 (.D(DATAL9), .en(LED9EN), .clk(CLK), .Q(LED9));  // open: clr
  Decoder #(.select(4)) decoder_1 (
    .out0(LED0END), .out1(LED1END), .out2(LED2END), .out3(LED3END), .out4(LED4END), .out5(LED5END),
    .out6(LED6END), .out7(LED7END), .out8(LED8END), .out9(LED9END), .out10(LEDAEND), .out11(LEDBEND),
    .out12(LEDCEND), .out13(LEDDEND), .out14(LEDEEND), .out15(LEDFEND), .sel(ADDR[3:0]), .en(and_1_out));
  or or_1 (LED0EN, LED0END, LEDFEND);
  or or_2 (LED1EN, LED1END, LEDFEND);
  or or_3 (LED2EN, LED2END, LEDFEND);
  or or_4 (LED3EN, LED3END, LEDFEND);
  or or_5 (LED4EN, LED4END, LEDFEND);
  or or_6 (LED5EN, LED5END, LEDFEND);
  or or_7 (LED6EN, LED6END, LEDFEND);
  or or_8 (LED7EN, LED7END, LEDFEND);
  or or_9 (LED8EN, LED8END, LEDFEND);
  or or_10 (LED9EN, LED9END, LEDFEND);
  or or_11 (LEDAEN, LEDAEND, LEDFEND);
  or or_12 (LEDBEN, LEDBEND, LEDFEND);
  or or_13 (LEDCEN, LEDCEND, LEDFEND);
  or or_14 (LEDDEN, LEDDEND, LEDFEND);
  or or_15 (LEDEEN, LEDEEND, LEDFEND);
  Pull_Resistor pull_resistor_1 (.node(KBDATA15[12]));
  Pull_Resistor pull_resistor_2 (.node(KBDATA15[11]));
  Pull_Resistor pull_resistor_3 (.node(KBDATA15[13]));
  Pull_Resistor pull_resistor_4 (.node(KBDATA15[14]));
  Register #(.width(15)) register_11 (.D(DATALA), .en(LEDAEN), .clk(CLK), .Q(LEDA));  // open: clr
  Register #(.width(15)) register_12 (.D(DATALB), .en(LEDBEN), .clk(CLK), .Q(LEDB));  // open: clr
  Register #(.width(15)) register_13 (.D(DATALC), .en(LEDCEN), .clk(CLK), .Q(LEDC));  // open: clr
  Register #(.width(15)) register_14 (.D(DATALD), .en(LEDDEN), .clk(CLK), .Q(LEDD));  // open: clr
  Register #(.width(15)) register_15 (.D(DATALE), .en(LEDEEN), .clk(CLK), .Q(LEDE));  // open: clr
  Pull_Resistor pull_resistor_5 (.node(KBDATA15[9]));
  Pull_Resistor pull_resistor_6 (.node(KBDATA15[10]));
  Pull_Resistor pull_resistor_7 (.node(DATA7));
  Pull_Resistor pull_resistor_8 (.node(KBDATA15[8]));
  Multiplexer #(.width(15), .enable("false")) multiplexer_1 (.in0(CPUDATAIN), .in1(LED1), .out(DATAL0), .sel(LEDFEND));
  Multiplexer #(.width(15), .enable("false")) multiplexer_2 (.in0(CPUDATAIN), .in1(LED2), .out(DATAL1), .sel(LEDFEND));
  Multiplexer #(.width(15), .enable("false")) multiplexer_3 (.in0(CPUDATAIN), .in1(LED3), .out(DATAL2), .sel(LEDFEND));
  Multiplexer #(.width(15), .enable("false")) multiplexer_4 (.in0(CPUDATAIN), .in1(LED4), .out(DATAL3), .sel(LEDFEND));
  Multiplexer #(.width(15), .enable("false")) multiplexer_5 (.in0(CPUDATAIN), .in1(LED5), .out(DATAL4), .sel(LEDFEND));
  Controlled_Buffer controlled_buffer_4 (.out(controlled_buffer_4_out));  // open: in, en
  Multiplexer #(.select(4), .width(15)) multiplexer_6 (
    .in0(LED0), .in1(LED1), .in2(LED2), .in3(LED3), .in4(LED4), .in5(LED5), .in6(LED6), .in7(LED7),
    .in8(LED8), .in9(LED9), .in10(LEDA), .in11(LEDB), .in12(LEDC), .in13(LEDD), .in14(LEDE),
    .in15({15{1'b0}}), .out(LEDDATA), .sel(ADDR[3:0]), .en(LEDRE));
  Multiplexer #(.width(15), .enable("false")) multiplexer_7 (.in0(CPUDATAIN), .in1(LED6), .out(DATAL5), .sel(LEDFEND));
  Multiplexer #(.width(15), .enable("false")) multiplexer_8 (.in0(CPUDATAIN), .in1(LED7), .out(DATAL6), .sel(LEDFEND));
  Multiplexer #(.width(15), .enable("false")) multiplexer_9 (.in0(CPUDATAIN), .in1(LED8), .out(DATAL7), .sel(LEDFEND));
  Multiplexer #(.width(15), .enable("false")) multiplexer_10 (.in0(CPUDATAIN), .in1(LED9), .out(DATAL8), .sel(LEDFEND));
  Multiplexer #(.width(15), .enable("false")) multiplexer_11 (.in0(CPUDATAIN), .in1(LEDA), .out(DATAL9), .sel(LEDFEND));
  and and_2 (LEDRE, RE, LEDCS);
  Multiplexer #(.width(15), .enable("false")) multiplexer_12 (.in0(CPUDATAIN), .in1(LEDB), .out(DATALA), .sel(LEDFEND));
  Multiplexer #(.width(15), .enable("false")) multiplexer_13 (.in0(CPUDATAIN), .in1(LEDC), .out(DATALB), .sel(LEDFEND));
  Multiplexer #(.width(15), .enable("false")) multiplexer_14 (.in0(CPUDATAIN), .in1(LEDD), .out(DATALC), .sel(LEDFEND));
  Multiplexer #(.width(15), .enable("false")) multiplexer_15 (.in0(CPUDATAIN), .in1(LEDE), .out(DATALD), .sel(LEDFEND));
  Multiplexer #(.width(15), .enable("false")) multiplexer_16 (
    .in0(CPUDATAIN), .in1(CPUDATAIN), .out(DATALE), .sel(LEDFEND));
  and and_3 (IOCS, ADDR[5], ADDR[6], ADDR[7], ADDR[8], ADDR[9], ADDR[10], ADDR[11], ADDR[12], ADDR[13], ADDR[14], 1'b1);
  and and_4 (TTYCS, IOCS, ADDR[0], ~ADDR[1], ~ADDR[2], ~ADDR[3], ADDR[4]);  // AND_Gate
  and and_5 (KBCS, IOCS, ~ADDR[0], ~ADDR[1], ~ADDR[2], ~ADDR[3], ADDR[4]);  // AND_Gate
  and and_6 (IVECTADDR, ADDR[0], ADDR[1], ADDR[2], ADDR[3], ADDR[4], ADDR[5], ADDR[6], ADDR[7], ADDR[8], ADDR[9], ADDR[10], ADDR[11], ADDR[12], ADDR[13], ADDR[14]);
  and and_7 (TTYWR, TTYCS, WE);
  and and_8 (and_8_out, TTYWR, DATA7);
  and and_9 (KBRD, KBCS, RE);
  and and_10 (and_10_out, KBCS, WE);
  Multiplexer #(.enable("false")) multiplexer_17 (.in0(and_10_out), .in1(1'b0), .out(multiplexer_17_out), .sel(KBCLR));
  and and_11 (LEDCS, IOCS, ~ADDR[4], RWE);  // AND_Gate
  Register #(.width(15)) register_16 (.D(CPUDATAIN), .en(IVECTEN), .clk(CLK), .Q(IVECT));  // open: clr
  and and_12 (IVECTEN, IVECTADDR, WE);
  and and_13 (IVECTRE, IVECTADDR, RE);
  or or_16 (RWE, RE, WE);
  and and_14 (MEMCS, ~IOCS, RWE);  // AND_Gate
  Multiplexer #(.enable("false")) multiplexer_18 (.in0(and_8_out), .in1(1'b0), .out(multiplexer_18_out), .sel(TTYCLR));
  D_Flip_Flop d_ff_1 (.D(multiplexer_17_out), .clk(CLK), .Q(KBCLR));  // open: Qn, preset, reset
  D_Flip_Flop d_ff_2 (.D(multiplexer_18_out), .clk(CLK), .Q(TTYCLR));  // open: Qn, preset, reset
  D_Flip_Flop d_ff_3 (.D(multiplexer_19_out), .clk(CLK), .Q(d_ff_3_q));  // open: Qn, preset, reset
  Multiplexer #(.enable("false")) multiplexer_19 (.in0(undriven), .in1(1'b0), .out(multiplexer_19_out), .sel(d_ff_3_q));

  assign IRQ = KBIRQ;
  assign TTYDATA = CPUDATAIN[6:0];

  // Other names for the same wires on the sheet: DATA[14:0] = CPUDATAIN; KBDATA15[7:0] = {DATA7, KBDATA}
endmodule

module ADDER15 (
  input  [14:0] A,
  input  [14:0] B,
  input  CIN,
  output COUT,
  output [14:0] S
);

  wire p5_1_cout, p5_2_cout;

  P5 p5_1 (.COUT(p5_1_cout), .A(B[4:0]), .B(A[4:0]), .CIN(CIN));
  ADDER5 adder5_1 (.A(B[4:0]), .B(A[4:0]), .S(S[4:0]), .CIN(CIN));  // open: COUT
  P5 p5_2 (.COUT(p5_2_cout), .A(B[9:5]), .B(A[9:5]), .CIN(p5_1_cout));
  ADDER5 adder5_2 (.A(B[9:5]), .B(A[9:5]), .S(S[9:5]), .CIN(p5_1_cout));  // open: COUT
  ADDER5 adder5_3 (.COUT(COUT), .A(B[14:10]), .B(A[14:10]), .S(S[14:10]), .CIN(p5_2_cout));
endmodule

module REGS15 (
  input  [14:0] D,
  input  W,
  input  [2:0] SelD,
  input  CLK,
  input  [2:0] SelA,
  input  [2:0] SelB,
  output [14:0] R0,
  output [14:0] R1,
  output [14:0] R2,
  output [14:0] R3,
  output [14:0] R4,
  output [14:0] R5,
  output [14:0] R6,
  output [14:0] R7,
  output [14:0] A,
  output [14:0] B
);

  wire w1, w2, w3, w4, w5, w6, w7;

  Multiplexer #(.select(3), .width(15), .enable("false")) multiplexer_1 (
    .in0({15{1'b0}}), .in1(R1), .in2(R2), .in3(R3), .in4(R4), .in5(R5), .in6(R6), .in7(R7), .out(A),
    .sel(SelA));
  Decoder #(.select(3)) decoder_1 (
    .out1(w1), .out2(w2), .out3(w3), .out4(w4), .out5(w5), .out6(w6), .out7(w7), .sel(SelD), .en(W));  // open: out0
  Multiplexer #(.select(3), .width(15), .enable("false")) multiplexer_2 (
    .in0({15{1'b0}}), .in1(R1), .in2(R2), .in3(R3), .in4(R4), .in5(R5), .in6(R6), .in7(R7), .out(B),
    .sel(SelB));
  Register #(.width(15)) register_1 (.D(D), .en(w1), .clk(CLK), .Q(R1));  // open: clr
  Register #(.width(15)) register_2 (.D(D), .en(w2), .clk(CLK), .Q(R2));  // open: clr
  Register #(.width(15)) register_3 (.D(D), .en(w3), .clk(CLK), .Q(R3));  // open: clr
  Register #(.width(15)) register_4 (.D(D), .en(w4), .clk(CLK), .Q(R4));  // open: clr
  Register #(.width(15)) register_5 (.D(D), .en(w5), .clk(CLK), .Q(R5));  // open: clr
  Register #(.width(15)) register_6 (.D(D), .en(w6), .clk(CLK), .Q(R6));  // open: clr
  Register #(.width(15)) register_7 (.D(D), .en(w7), .clk(CLK), .Q(R7));  // open: clr

  assign R0 = {15{1'b0}};
endmodule

module ALU15 (
  input  [14:0] A,
  input  [14:0] B,
  input  [2:0] OP,
  input  CIN,
  input  OIN,
  output C,
  output O,
  output N,
  output Z,
  output [14:0] R,
  output [14:0] R_2
);

  wire adder15_1_cout, addsub, \and , and_1_out, and_2_out, and_4_out, and_5_out, and_6_out, decoder_1_out1,
       decoder_1_out2, decoder_1_out3, demultiplexer_2_out1, multiplexer_6_out, multiplexer_7_out, not_3_out,
       \or , or_3_out, shift, \xor ;
  wire [0:0] multiplexer_2_out, multiplexer_2_out_2, multiplexer_2_out_3, multiplexer_2_out_4,
       multiplexer_2_out_5, multiplexer_2_out_6, multiplexer_2_out_7, multiplexer_2_out_8,
       multiplexer_2_out_9, multiplexer_2_out_10, multiplexer_2_out_11, multiplexer_2_out_12,
       multiplexer_2_out_13, multiplexer_2_out_14, multiplexer_2_out_15;
  wire [3:0] multiplexer_5_out, not_2_out;
  wire [14:0] adder15_1_s, and_3_out, bit_extender_1_out, multiplexer_1_out, multiplexer_3_out, not_1_out,
       or_1_out, xor_1_out;
  wire [16:0] multiplexer_4_out;

  and and_1 (and_1_out, A[14], OP[0], OP[1]);
  assign bit_extender_1_out = {{14{and_1_out}}, and_1_out};  // Bit_Extender bit_extender_1
  Multiplexer #(.width(15), .enable("false")) multiplexer_1 (
    .in0(A), .in1(bit_extender_1_out), .out(multiplexer_1_out), .sel(OP[1]));
  and and_2 (and_2_out, Z, adder15_1_cout);
  assign C = addsub ? and_2_out : 1'bz;  // Controlled_Buffer controlled_buffer_1
  ADDER15 adder15_1 (.COUT(adder15_1_cout), .B(multiplexer_3_out), .A(A), .CIN(OP[0]), .S(adder15_1_s));
  assign {N, R[13:0]} = addsub ? adder15_1_s : 15'bz;  // Controlled_Buffer controlled_buffer_2
  Multiplexer #(.width(15), .enable("false")) multiplexer_2 (
    .in0(bit_extender_1_out), .in1(A),
    .out({multiplexer_2_out_10[0], multiplexer_2_out_9[0], multiplexer_2_out_8[0], multiplexer_2_out_7[0], multiplexer_2_out_6[0], multiplexer_2_out_5[0], multiplexer_2_out_4[0], multiplexer_2_out_3[0], multiplexer_2_out_2[0], multiplexer_2_out[0], multiplexer_2_out_11[0], multiplexer_2_out_12[0], multiplexer_2_out_13[0], multiplexer_2_out_14[0], multiplexer_2_out_15[0]}),
    .sel(OP[1]));
  assign not_1_out = ~B;  // NOT_Gate not_1, 15 bits wide
  Multiplexer #(.width(15), .enable("false")) multiplexer_3 (
    .in0(B), .in1(not_1_out), .out(multiplexer_3_out), .sel(OP[0]));
  Multiplexer #(.select(4), .width(17), .enable("false")) multiplexer_4 (
    .in0({multiplexer_1_out[0], multiplexer_2_out_10[0], multiplexer_2_out_9[0], multiplexer_2_out_8[0], multiplexer_2_out_7[0], multiplexer_2_out_6[0], multiplexer_2_out_5[0], multiplexer_2_out_4[0], multiplexer_2_out_3[0], multiplexer_2_out_2[0], multiplexer_2_out[0], multiplexer_2_out_11[0], multiplexer_2_out_12[0], multiplexer_2_out_13[0], multiplexer_2_out_14[0], multiplexer_2_out_15[0], 1'b0}),
    .in1({multiplexer_1_out[1:0], multiplexer_2_out_10[0], multiplexer_2_out_9[0], multiplexer_2_out_8[0], multiplexer_2_out_7[0], multiplexer_2_out_6[0], multiplexer_2_out_5[0], multiplexer_2_out_4[0], multiplexer_2_out_3[0], multiplexer_2_out_2[0], multiplexer_2_out[0], multiplexer_2_out_11[0], multiplexer_2_out_12[0], multiplexer_2_out_13[0], multiplexer_2_out_14[0], multiplexer_2_out_15[0]}),
    .in2({multiplexer_1_out[2:0], multiplexer_2_out_10[0], multiplexer_2_out_9[0], multiplexer_2_out_8[0], multiplexer_2_out_7[0], multiplexer_2_out_6[0], multiplexer_2_out_5[0], multiplexer_2_out_4[0], multiplexer_2_out_3[0], multiplexer_2_out_2[0], multiplexer_2_out[0], multiplexer_2_out_11[0], multiplexer_2_out_12[0], multiplexer_2_out_13[0], multiplexer_2_out_14[0]}),
    .in3({multiplexer_1_out[3:0], multiplexer_2_out_10[0], multiplexer_2_out_9[0], multiplexer_2_out_8[0], multiplexer_2_out_7[0], multiplexer_2_out_6[0], multiplexer_2_out_5[0], multiplexer_2_out_4[0], multiplexer_2_out_3[0], multiplexer_2_out_2[0], multiplexer_2_out[0], multiplexer_2_out_11[0], multiplexer_2_out_12[0], multiplexer_2_out_13[0]}),
    .in4({multiplexer_1_out[4:0], multiplexer_2_out_10[0], multiplexer_2_out_9[0], multiplexer_2_out_8[0], multiplexer_2_out_7[0], multiplexer_2_out_6[0], multiplexer_2_out_5[0], multiplexer_2_out_4[0], multiplexer_2_out_3[0], multiplexer_2_out_2[0], multiplexer_2_out[0], multiplexer_2_out_11[0], multiplexer_2_out_12[0]}),
    .in5({multiplexer_1_out[5:0], multiplexer_2_out_10[0], multiplexer_2_out_9[0], multiplexer_2_out_8[0], multiplexer_2_out_7[0], multiplexer_2_out_6[0], multiplexer_2_out_5[0], multiplexer_2_out_4[0], multiplexer_2_out_3[0], multiplexer_2_out_2[0], multiplexer_2_out[0], multiplexer_2_out_11[0]}),
    .in6({multiplexer_1_out[6:0], multiplexer_2_out_10[0], multiplexer_2_out_9[0], multiplexer_2_out_8[0], multiplexer_2_out_7[0], multiplexer_2_out_6[0], multiplexer_2_out_5[0], multiplexer_2_out_4[0], multiplexer_2_out_3[0], multiplexer_2_out_2[0], multiplexer_2_out[0]}),
    .in7({multiplexer_1_out[7:0], multiplexer_2_out_10[0], multiplexer_2_out_9[0], multiplexer_2_out_8[0], multiplexer_2_out_7[0], multiplexer_2_out_6[0], multiplexer_2_out_5[0], multiplexer_2_out_4[0], multiplexer_2_out_3[0], multiplexer_2_out_2[0]}),
    .in8({multiplexer_1_out[8:0], multiplexer_2_out_10[0], multiplexer_2_out_9[0], multiplexer_2_out_8[0], multiplexer_2_out_7[0], multiplexer_2_out_6[0], multiplexer_2_out_5[0], multiplexer_2_out_4[0], multiplexer_2_out_3[0]}),
    .in9({multiplexer_1_out[9:0], multiplexer_2_out_10[0], multiplexer_2_out_9[0], multiplexer_2_out_8[0], multiplexer_2_out_7[0], multiplexer_2_out_6[0], multiplexer_2_out_5[0], multiplexer_2_out_4[0]}),
    .in10({multiplexer_1_out[10:0], multiplexer_2_out_10[0], multiplexer_2_out_9[0], multiplexer_2_out_8[0], multiplexer_2_out_7[0], multiplexer_2_out_6[0], multiplexer_2_out_5[0]}),
    .in11({multiplexer_1_out[11:0], multiplexer_2_out_10[0], multiplexer_2_out_9[0], multiplexer_2_out_8[0], multiplexer_2_out_7[0], multiplexer_2_out_6[0]}),
    .in12({multiplexer_1_out[12:0], multiplexer_2_out_10[0], multiplexer_2_out_9[0], multiplexer_2_out_8[0], multiplexer_2_out_7[0]}),
    .in13({multiplexer_1_out[13:0], multiplexer_2_out_10[0], multiplexer_2_out_9[0], multiplexer_2_out_8[0]}),
    .in14({multiplexer_1_out, multiplexer_2_out_10[0], multiplexer_2_out_9[0]}),
    .in15({1'b0, multiplexer_1_out, multiplexer_2_out_10[0]}), .out(multiplexer_4_out),
    .sel(multiplexer_5_out));
  // Probe on multiplexer_5_out
  Multiplexer #(.width(4), .enable("false")) multiplexer_5 (
    .in0(not_2_out), .in1(B[3:0]), .out(multiplexer_5_out), .sel(OP[1]));
  assign not_2_out = ~B[3:0];  // NOT_Gate not_2, 4 bits wide
  Multiplexer #(.enable("false")) multiplexer_6 (
    .in0(multiplexer_4_out[16]), .in1(multiplexer_4_out[0]), .out(multiplexer_6_out), .sel(OP[1]));
  // Probe on multiplexer_4_out[15:1]
  assign and_3_out = A & B;  // AND_Gate and_3, 15 bits wide
  assign or_1_out = A | B;  // OR_Gate or_1, 15 bits wide
  assign xor_1_out = A ^ B;  // XOR_Gate xor_1, 15 bits wide
  assign C = shift ? multiplexer_6_out : 1'bz;  // Controlled_Buffer controlled_buffer_3
  assign {N, R[13:0]} = shift ? multiplexer_4_out[15:1] : 15'bz;  // Controlled_Buffer controlled_buffer_4
  assign {N, R[13:0]} = \and  ? and_3_out : 15'bz;  // Controlled_Buffer controlled_buffer_5
  assign {N, R[13:0]} = \or  ? or_1_out : 15'bz;  // Controlled_Buffer controlled_buffer_6
  assign {N, R[13:0]} = \xor  ? xor_1_out : 15'bz;  // Controlled_Buffer controlled_buffer_7
  Decoder #(.select(2)) decoder_1 (
    .out0(addsub), .out1(decoder_1_out1), .out2(decoder_1_out2), .out3(decoder_1_out3), .sel(OP[2:1]),
    .en(1'b1));
  Demultiplexer #(.enable("false")) demultiplexer_1 (.out0(\and ), .out1(\or ), .in(decoder_1_out1), .sel(OP[0]));
  Demultiplexer #(.enable("false")) demultiplexer_2 (
    .out0(\xor ), .out1(demultiplexer_2_out1), .in(decoder_1_out2), .sel(OP[0]));
  or or_2 (shift, demultiplexer_2_out1, decoder_1_out3);
  nor nor_1 (Z, R[0], R[1], R[2], R[3], R[4], R[5], R[6], R[7], R[8], R[9], R[10], R[11], R[12], R[13], N);
  Multiplexer #(.enable("false")) multiplexer_7 (.in0(B[14]), .in1(not_3_out), .out(multiplexer_7_out), .sel(OP[0]));
  not not_3 (not_3_out, B[14]);
  and and_4 (and_4_out, multiplexer_7_out, A[14]);
  and and_5 (and_5_out, and_4_out, ~N);  // AND_Gate
  or or_3 (or_3_out, multiplexer_7_out, A[14]);
  and and_6 (and_6_out, N, ~or_3_out);  // AND_Gate
  or or_4 (O, and_6_out, and_5_out);

  assign R[14] = N;
  assign R_2 = {N, R[13:0]};

  // Other names for the same wires on the sheet: o0 = OP[0]; o1 = OP[1]
endmodule

module FLAGS8 (
  input  IRQ,
  input  [7:0] NF,
  input  [7:0] WM,
  input  CLK,
  output [7:0] F
);

  wire and_1_out, d_ff_1_qn, E, multiplexer_1_out, multiplexer_4_out, undriven;
  wire [7:0] multiplexer_8_out;

  D_Flip_Flop d_ff_1 (.D(and_1_out), .clk(CLK), .Qn(d_ff_1_qn));  // open: Q, preset, reset
  and and_1 (and_1_out, IRQ, E);
  Multiplexer #(.enable("false")) multiplexer_1 (.in0(F[6]), .in1(NF[6]), .out(multiplexer_1_out), .sel(WM[6]));
  Multiplexer #(.enable("false")) multiplexer_2 (.in0(F[7]), .in1(NF[7]), .out(multiplexer_8_out[7]), .sel(WM[7]));
  Pull_Resistor pull_resistor_1 (.node(E));
  assign E = d_ff_1_qn ? multiplexer_4_out : 1'bz;  // Controlled_Buffer controlled_buffer_1
  Multiplexer #(.enable("false")) multiplexer_3 (.in0(F[4]), .in1(NF[4]), .out(multiplexer_8_out[4]), .sel(WM[4]));
  Multiplexer #(.enable("false")) multiplexer_4 (.in0(F[5]), .in1(NF[5]), .out(multiplexer_4_out), .sel(WM[5]));
  Multiplexer #(.enable("false")) multiplexer_5 (.in0(F[2]), .in1(NF[2]), .out(multiplexer_8_out[2]), .sel(WM[2]));
  Multiplexer #(.enable("false")) multiplexer_6 (.in0(F[3]), .in1(NF[3]), .out(multiplexer_8_out[3]), .sel(WM[3]));
  Multiplexer #(.enable("false")) multiplexer_7 (.in0(F[1]), .in1(NF[1]), .out(multiplexer_8_out[1]), .sel(WM[1]));
  Multiplexer #(.enable("false")) multiplexer_8 (.in0(F[0]), .in1(NF[0]), .out(multiplexer_8_out[0]), .sel(WM[0]));
  Register register_1 (
    .D({multiplexer_8_out[7], IRQ, E, multiplexer_8_out[4:0]}), .en(undriven), .clk(CLK), .Q(F));  // open: clr
endmodule

module IMM15 (
  input  [14:0] INST,
  output [14:0] SEXT
);
endmodule

module DECODE15 (
  input  [4:0] OPCODE,
  output SWI,
  output STORE,
  output LOAD,
  output [1:0] ASEL,
  output [1:0] BSEL,
  output [2:0] ALUOP,
  output [2:0] REGDATASRC,
  output REGW,
  output [1:0] FLAGSRC,
  output [7:0] FLAGWM,
  output SRPW,
  output SRFW,
  output [1:0] PWSRC
);

  wire ALL, ALU, ALu_t, alU_t_t, ALuf, and_1_out, C, controlled_buffer_13_out, controlled_buffer_14_out,
       decoder_1_out0, decoder_1_out1, decoder_1_out2, decoder_2_out1, decoder_2_out2, decoder_2_out3,
       decoder_2_out4, decoder_2_out5, decoder_2_out6, decoder_2_out7, decoder_2_out8, decoder_2_out10,
       decoder_2_out11, decoder_2_out12, decoder_2_out13, decoder_2_out14, decoder_2_out15, decoder_2_out16,
       decoder_2_out17, decoder_2_out18, decoder_2_out19, decoder_2_out20, decoder_2_out21, decoder_2_out26,
       decoder_2_out27, decoder_2_out28, decoder_2_out29, decoder_2_out31, F, imm10, isr, isr2, isrlift, nop,
       not_1_out, not_2_out, not_3_out, not_4_out, not_5_out, not_6_out, not_7_out, not_8_out, or_4_out,
       or_5_out, or_6_out, or_7_out, PC, PCa1, PCaALU, rd, RTI, sr1, sr2, SRF, SRf_t, SRP, sRP_t, zero, zerof;
  wire [1:0] controlled_buffer_6_out, controlled_buffer_7_out;
  wire [2:0] controlled_buffer_5_out;
  wire [7:0] controlled_buffer_1_out;
  wire [7:1] FLAGWM_t;

  assign controlled_buffer_1_out = ALL ? {8{1'b1}} : 8'bz;  // Controlled_Buffer controlled_buffer_1
  not not_1 (not_1_out, ALL);
  assign controlled_buffer_1_out = not_1_out ? {FLAGWM_t[7:6], SWI, FLAGWM_t[4:3], C, {2{FLAGWM_t[1]}}} : 8'bz;  // Controlled_Buffer controlled_buffer_2
  assign FLAGWM = not_2_out ? controlled_buffer_1_out : 8'bz;  // Controlled_Buffer controlled_buffer_3
  not not_2 (not_2_out, nop);
  Decoder #(.select(2)) decoder_1 (
    .out0(decoder_1_out0), .out1(decoder_1_out1), .out2(decoder_1_out2), .sel(OPCODE[4:3]));  // open: out3, en
  Pull_Resistor pull_resistor_1 (.node(FLAGWM));
  assign BSEL = decoder_1_out1 ? 2'b01 : 2'bz;  // Controlled_Buffer controlled_buffer_4
  Pull_Resistor pull_resistor_2 (.node(SWI));
  Pull_Resistor pull_resistor_3 (.node(STORE));
  Pull_Resistor pull_resistor_4 (.node(LOAD));
  Pull_Resistor pull_resistor_5 (.node(ASEL));
  Pull_Resistor pull_resistor_6 (.node(BSEL));
  Pull_Resistor pull_resistor_7 (.node(ALUOP));
  Pull_Resistor pull_resistor_8 (.node(REGDATASRC));
  Pull_Resistor pull_resistor_9 (.node(REGW));
  Pull_Resistor pull_resistor_10 (.node(FLAGSRC));
  Pull_Resistor pull_resistor_11 (.node(SRPW));
  Pull_Resistor pull_resistor_12 (.node(SRFW));
  Pull_Resistor pull_resistor_13 (.node(PWSRC));
  or or_1 (FLAGWM_t[1], decoder_1_out0, decoder_1_out1);
  assign controlled_buffer_5_out = FLAGWM_t[1] ? OPCODE[2:0] : 3'bz;  // Controlled_Buffer controlled_buffer_5
  not not_3 (not_3_out, LOAD);
  // Probe on OPCODE
  assign controlled_buffer_6_out = decoder_1_out2 ? 2'b11 : 2'bz;  // Controlled_Buffer controlled_buffer_6
  not not_4 (not_4_out, SWI);
  assign controlled_buffer_7_out = not_4_out ? controlled_buffer_6_out : 2'bz;  // Controlled_Buffer controlled_buffer_7
  not not_5 (not_5_out, RTI);
  assign PWSRC = RTI ? 2'b10 : 2'bz;  // Controlled_Buffer controlled_buffer_8
  assign PWSRC = not_5_out ? controlled_buffer_7_out : 2'bz;  // Controlled_Buffer controlled_buffer_9
  and and_1 (and_1_out, OPCODE[2], FLAGWM_t[1]);
  assign ALUOP = not_3_out ? controlled_buffer_5_out : 3'bz;  // Controlled_Buffer controlled_buffer_10
  assign ASEL = decoder_1_out2 ? 2'b01 : 2'bz;  // Controlled_Buffer controlled_buffer_11
  assign BSEL = decoder_1_out2 ? 2'b10 : 2'bz;  // Controlled_Buffer controlled_buffer_12
  not not_6 (not_6_out, LOAD);
  assign controlled_buffer_13_out = not_6_out ? 1'b1 : 1'bz;  // Controlled_Buffer controlled_buffer_13
  not not_7 (not_7_out, STORE);
  assign controlled_buffer_14_out = not_7_out ? controlled_buffer_13_out : 1'bz;  // Controlled_Buffer controlled_buffer_14
  not not_8 (not_8_out, decoder_1_out2);
  assign REGW = not_8_out ? controlled_buffer_14_out : 1'bz;  // Controlled_Buffer controlled_buffer_15
  or or_2 (FLAGWM_t[3], nop, decoder_2_out1, decoder_2_out8);
  or or_3 (C, and_1_out, FLAGWM_t[3]);
  Decoder #(.select(5)) decoder_2 (
    .out0(nop), .out1(decoder_2_out1), .out2(decoder_2_out2), .out3(decoder_2_out3), .out4(decoder_2_out4),
    .out5(decoder_2_out5), .out6(decoder_2_out6), .out7(decoder_2_out7), .out8(decoder_2_out8), .out9(LOAD),
    .out10(decoder_2_out10), .out11(decoder_2_out11), .out12(decoder_2_out12), .out13(decoder_2_out13),
    .out14(decoder_2_out14), .out15(decoder_2_out15), .out16(decoder_2_out16), .out17(decoder_2_out17),
    .out18(decoder_2_out18), .out19(decoder_2_out19), .out20(decoder_2_out20), .out21(decoder_2_out21),
    .out22(RTI), .out23(SWI), .out24(SRPW), .out25(SRFW), .out26(decoder_2_out26), .out27(decoder_2_out27),
    .out28(decoder_2_out28), .out29(decoder_2_out29), .out30(STORE), .out31(decoder_2_out31), .sel(OPCODE));  // open: en
  Decoder #(.select(2)) decoder_3 (.out0(sr2), .out1(isr2), .out2(zero), .out3(rd), .sel(BSEL));  // open: en
  Decoder #(.select(2)) decoder_4 (.out0(sr1), .out1(imm10), .out2(isrlift), .out3(isr), .sel(ASEL));  // open: en
  Decoder #(.select(3)) decoder_5 (
    .out0(ALU), .out1(SRP), .out2(SRF), .out3(PC), .out4(F), .sel(REGDATASRC));  // open: out5, out6, out7, en
  Decoder #(.select(2)) decoder_6 (.out0(PCa1), .out1(alU_t_t), .out2(sRP_t), .out3(PCaALU), .sel(PWSRC));  // open: en
  Decoder #(.select(2)) decoder_7 (.out0(ALuf), .out1(ALu_t), .out2(zerof), .out3(SRf_t), .sel(FLAGSRC));  // open: en
  or or_4 (or_4_out, decoder_2_out29, decoder_2_out28);
  or or_5 (or_5_out, decoder_2_out29, decoder_2_out26);
  or or_6 (or_6_out, decoder_2_out31, or_4_out);
  assign BSEL = STORE ? 2'b11 : 2'bz;  // Controlled_Buffer controlled_buffer_16
  or or_7 (or_7_out, decoder_2_out26, decoder_2_out29);
  assign BSEL = decoder_2_out27 ? 2'b01 : 2'bz;  // Controlled_Buffer controlled_buffer_17
  assign BSEL = or_6_out ? 2'b10 : 2'bz;  // Controlled_Buffer controlled_buffer_18
  assign FLAGSRC = SWI ? 2'b10 : 2'bz;  // Controlled_Buffer controlled_buffer_19
  assign FLAGSRC = RTI ? 2'b11 : 2'bz;  // Controlled_Buffer controlled_buffer_20
  assign PWSRC = decoder_2_out27 ? 2'b01 : 2'bz;  // Controlled_Buffer controlled_buffer_21
  assign FLAGSRC = or_5_out ? 2'b01 : 2'bz;  // Controlled_Buffer controlled_buffer_22
  assign ASEL = decoder_2_out31 ? 2'b10 : 2'bz;  // Controlled_Buffer controlled_buffer_23
  assign ASEL = or_4_out ? 2'b11 : 2'bz;  // Controlled_Buffer controlled_buffer_24
  assign REGDATASRC = SRPW ? 3'b001 : 3'bz;  // Controlled_Buffer controlled_buffer_25
  assign REGDATASRC = SRFW ? 3'b010 : 3'bz;  // Controlled_Buffer controlled_buffer_26
  assign PWSRC = decoder_2_out28 ? 2'b11 : 2'bz;  // Controlled_Buffer controlled_buffer_27
  assign REGDATASRC = decoder_2_out28 ? 3'b011 : 3'bz;  // Controlled_Buffer controlled_buffer_28
  assign REGDATASRC = or_7_out ? 3'b100 : 3'bz;  // Controlled_Buffer controlled_buffer_29
  or or_8 (ALL, or_5_out, RTI);

  // Other names for the same wires on the sheet: FLAGWM_t (some bits) = {SWI, C, FLAGWM_t[1]}; ZN = FLAGWM_t[1];
  //   O = FLAGWM_t[3]; E = SWI; I = FLAGWM_t[6]
endmodule

module FA (
  input  X,
  input  Y,
  input  Cin,
  output S,
  output C
);

  wire and_1_out, and_2_out, and_3_out;

  and and_1 (and_1_out, Cin, X);
  and and_2 (and_2_out, Cin, Y);
  and and_3 (and_3_out, Y, X);
  or or_1 (C, and_3_out, and_2_out, and_1_out);
  xor xor_1 (S, X, Y, Cin);
endmodule

module ADDER5 (
  input  [4:0] A,
  input  [4:0] B,
  input  CIN,
  output COUT,
  output [4:0] S
);

  wire fa_1_c, fa_2_c, fa_3_c, fa_4_c;

  FA fa_1 (.X(A[0]), .Y(B[0]), .Cin(CIN), .S(S[0]), .C(fa_1_c));
  FA fa_2 (.X(A[2]), .Y(B[2]), .Cin(fa_3_c), .S(S[2]), .C(fa_2_c));
  FA fa_3 (.X(A[1]), .Y(B[1]), .Cin(fa_1_c), .S(S[1]), .C(fa_3_c));
  FA fa_4 (.X(A[3]), .Y(B[3]), .Cin(fa_2_c), .S(S[3]), .C(fa_4_c));
  FA fa_5 (.X(A[4]), .Y(B[4]), .Cin(fa_4_c), .S(S[4]), .C(COUT));
endmodule

module P5 (
  input  [4:0] A,
  input  [4:0] B,
  input  CIN,
  output COUT
);

  wire and_1_out, and_2_out, and_3_out, and_4_out, and_5_out;
  wire [4:0] and_6_out, xor_1_out;

  assign xor_1_out = A ^ B;  // XOR_Gate xor_1, 5 bits wide
  and and_1 (and_1_out, xor_1_out[4], xor_1_out[3], xor_1_out[2], xor_1_out[1], xor_1_out[0], CIN);
  and and_2 (and_2_out, xor_1_out[4], xor_1_out[3], xor_1_out[2], xor_1_out[1], and_6_out[0]);
  and and_3 (and_3_out, xor_1_out[4], xor_1_out[3], xor_1_out[2], and_6_out[1]);
  and and_4 (and_4_out, xor_1_out[4], and_6_out[3]);
  and and_5 (and_5_out, xor_1_out[4], xor_1_out[3], and_6_out[2]);
  assign and_6_out = A & B;  // AND_Gate and_6, 5 bits wide
  or or_1 (COUT, and_6_out[4], and_4_out, and_5_out, and_3_out, and_2_out, and_1_out);
endmodule

module alu (
  input  in_1,
  input  in_2
);

  wire d_ff_1_q, d_ff_2_q, PCa1;
  wire [14:0] PC, register_1_q;

  D_Flip_Flop d_ff_1 (.D(in_2), .clk(in_1), .Q(d_ff_1_q));  // open: Qn, preset, reset
  D_Flip_Flop d_ff_2 (.D(d_ff_1_q), .clk(in_1), .Q(d_ff_2_q));  // open: Qn, preset, reset
  Register #(.width(15)) register_1 (.D({15{1'b1}}), .clk(in_1), .Q(register_1_q));  // open: en, clr
  Counter #(.width(15), .max('h7fff)) counter_1 (
    .load(d_ff_2_q), .up(1'b1), .count(PCa1), .clk(in_1), .D(register_1_q), .Q(PC));  // open: clr, carry

  // Other names for the same wires on the sheet: CLK = in_1
endmodule

module cpu (
  input  [14:0] DATAIN,
  input  CLK,
  input  IRQ,
  output [14:0] PC,
  output [14:0] IB,
  output [14:0] SRP,
  output [7:0] SRF,
  output [14:0] R0,
  output [14:0] R1,
  output [14:0] R2,
  output [14:0] R3,
  output [14:0] R4,
  output [14:0] R5,
  output [14:0] R6,
  output [14:0] R7,
  output RE,
  output WE,
  output I,
  output Z,
  output [14:0] ADDR,
  output N,
  output O,
  output C,
  output E,
  output [14:0] DATAOUT
);

  wire a1, ALu_t, alU_t_t, ALuf, and_1_out, and_3_out, and_6_out, and_7_out, count, counter_1_carry,
       d_ff_3_q, decoder_2_out3, decoder_6_out2, forward, jump, jumpin, KLC, load, multiplexer_4_out,
       not_2_out, not_3_out, not_4_out, not_6_out, not_7_out, not_8_out, not_10_out, not_11_out, or_1_out,
       or_2_out, or_4_out, or_5_out, or_6_out, regW, SRf_t, SRFW, sRP_t, SRPW, stLOAD, stSTORE, SWI,
       t_ff_1_q, t_ff_2_q, tALU, tF, tird, tisr, tisr2, tisrlift, tPC, tsr1, tsr2, tSRF, tSRP, tzero,
       undriven, undriven_2;
  wire [0:0] decode15_1_aluop;
  wire [1:0] decode15_1_asel, decode15_1_bsel, decode15_1_flagsrc, decode15_1_pwsrc;
  wire [2:0] ALUOP, controlled_buffer_20_out, decode15_1_regdatasrc, register_5_q;
  wire [3:0] alu15_1_z, decode15_1_flagwm, multiplexer_5_out, not_9_out;
  wire [7:0] ALUFLAG, controlled_buffer_14_out, flagWm;
  wire [7:4] F;
  wire [14:0] adder15_1_s, ALU, bit_extender_2_out, bit_extender_3_out, bit_extender_4_out,
       bit_extender_6_out, bit_extender_7_out, controlled_buffer_4_out, controlled_buffer_8_out,
       controlled_buffer_11_out, controlled_buffer_17_out, controlled_buffer_19_out,
       controlled_buffer_26_out, DATA, DATAOUT_t, isr2, multiplexer_3_out, NPC, register_6_q, sr1, sr2;

  not not_1 (KLC, CLK);
  D_Flip_Flop d_ff_1 (.clk(stLOAD), .D(1'b0), .preset(load));  // open: Q, Qn, reset
  Multiplexer #(.enable("false")) multiplexer_1 (.in0(stLOAD), .in1(1'b0), .sel(load));  // open: out
  D_Flip_Flop d_ff_2 (.clk(stSTORE), .D(1'b0), .preset(WE));  // open: Q, Qn, reset
  Multiplexer #(.enable("false")) multiplexer_2 (.in0(stSTORE), .in1(1'b0), .sel(WE));  // open: out
  Register #(.width(15)) register_1 (.D(DATA), .en(forward), .clk(CLK), .Q(IB), .clr(d_ff_3_q));
  D_Flip_Flop d_ff_3 (.D(undriven), .Q(d_ff_3_q), .reset(d_ff_3_q));  // open: clk, Qn, preset
  assign DATAOUT_t = WE ? sr2 : 15'bz;  // Controlled_Buffer controlled_buffer_1
  Multiplexer #(.width(15), .enable("false")) multiplexer_3 (
    .in0(NPC), .in1(ALU), .out(multiplexer_3_out), .sel(or_1_out));
  or or_1 (or_1_out, stLOAD, and_1_out);
  and and_1 (and_1_out, stSTORE, forward);
  not not_2 (not_2_out, or_1_out);
  Register #(.width(15)) register_2 (.D(multiplexer_3_out), .clk(KLC), .Q(ADDR));  // open: en, clr
  assign DATA = RE ? DATAIN : 15'bz;  // Controlled_Buffer controlled_buffer_2
  assign DATAOUT = WE ? DATAOUT_t : 15'bz;  // Controlled_Buffer controlled_buffer_3
  // Probe on IB[13:11]
  // Probe on IB[14]
  // Probe on ADDR
  // Probe on DATAIN
  not not_3 (not_3_out, jumpin);
  not not_4 (not_4_out, WE);
  nor nor_1 (count, stLOAD, WE);
  assign isr2 = {{11{IB[14]}}, IB[14:11]};  // Bit_Extender bit_extender_1
  // Probe on IB[7:5]
  // Probe on IB[10:8]
  not not_5 (RE, WE);
  and and_2 (forward, not_3_out, not_4_out);
  // Probe on IB[4:0]
  // Probe on IB[14:8]
  assign controlled_buffer_4_out = tsr2 ? sr2 : 15'bz;  // Controlled_Buffer controlled_buffer_4
  assign controlled_buffer_4_out = tisr2 ? isr2 : 15'bz;  // Controlled_Buffer controlled_buffer_5
  assign controlled_buffer_4_out = tzero ? R0 : 15'bz;  // Controlled_Buffer controlled_buffer_6
  assign bit_extender_2_out = {{12{1'b0}}, IB[7:5]};  // Bit_Extender bit_extender_2
  assign controlled_buffer_4_out = tird ? bit_extender_2_out : 15'bz;  // Controlled_Buffer controlled_buffer_7
  assign controlled_buffer_8_out = SRPW ? ALU : 15'bz;  // Controlled_Buffer controlled_buffer_8
  assign controlled_buffer_8_out = SWI ? NPC : 15'bz;  // Controlled_Buffer controlled_buffer_9
  assign controlled_buffer_8_out = IRQ ? PC : 15'bz;  // Controlled_Buffer controlled_buffer_10
  Register #(.width(15)) register_3 (.D(controlled_buffer_8_out), .en(or_2_out), .clk(CLK), .Q(SRP));  // open: clr
  or or_2 (or_2_out, IRQ, SWI, SRPW);
  assign controlled_buffer_11_out = tsr1 ? sr1 : 15'bz;  // Controlled_Buffer controlled_buffer_11
  assign controlled_buffer_11_out = tisrlift ? bit_extender_3_out : 15'bz;  // Controlled_Buffer controlled_buffer_12
  assign bit_extender_3_out = {{4{IB[14]}}, {IB[14:8], 4'b0000}};  // Bit_Extender bit_extender_3
  assign controlled_buffer_11_out = tisr ? bit_extender_4_out : 15'bz;  // Controlled_Buffer controlled_buffer_13
  assign bit_extender_4_out = {{8{IB[14]}}, IB[14:8]};  // Bit_Extender bit_extender_4
  DECODE15 decode15_1 (
    .SWI(SWI), .FLAGWM({flagWm[7:4], decode15_1_flagwm}), .ALUOP({ALUOP[2:1], decode15_1_aluop[0]}),
    .BSEL(decode15_1_bsel), .SRFW(SRFW), .STORE(stSTORE), .FLAGSRC(decode15_1_flagsrc), .SRPW(SRPW),
    .REGW(regW), .OPCODE(IB[4:0]), .REGDATASRC(decode15_1_regdatasrc), .ASEL(decode15_1_asel), .LOAD(stLOAD),
    .PWSRC(decode15_1_pwsrc));
  Decoder #(.select(2)) decoder_1 (
    .out0(tsr2), .out1(tisr2), .out2(tzero), .out3(tird), .sel(decode15_1_bsel));  // open: en
  Decoder #(.select(2)) decoder_2 (
    .out0(a1), .out1(alU_t_t), .out2(sRP_t), .out3(decoder_2_out3), .sel(decode15_1_pwsrc), .en(undriven_2));
  Decoder #(.select(2)) decoder_3 (
    .out0(a1), .out1(alU_t_t), .out2(sRP_t), .out3(decoder_2_out3), .sel(decode15_1_pwsrc), .en(undriven_2));
  and and_3 (and_3_out, stSTORE, IB[14]);
  or or_3 (ALUOP[0], and_3_out, decode15_1_aluop[0]);
  not not_6 (not_6_out, Z);
  not not_7 (not_7_out, N);
  not not_8 (not_8_out, C);
  Decoder #(.select(2)) decoder_4 (.out0(tsr1), .out2(tisrlift), .out3(tisr), .sel(decode15_1_asel));  // open: out1, en
  Decoder #(.select(3)) decoder_5 (
    .out0(tALU), .out1(tSRP), .out2(tSRF), .out3(tPC), .out4(tF), .sel(decode15_1_regdatasrc));  // open: out5, out6, out7, en
  Decoder #(.select(2)) decoder_6 (
    .out0(ALuf), .out1(ALu_t), .out2(decoder_6_out2), .out3(SRf_t), .sel(decode15_1_flagsrc));  // open: en
  Multiplexer #(.select(3), .enable("false")) multiplexer_4 (
    .in0(Z), .in1(not_6_out), .in2(N), .in3(not_7_out), .in4(C), .in5(not_8_out), .in6(1'b0), .in7(1'b0),
    .out(multiplexer_4_out), .sel(IB[2:0]));
  // Probe on ALUOP
  // Probe on controlled_buffer_4_out
  ALU15 alu15_1 (
    .C(alu15_1_z[2]), .R_2(ALU), .N(alu15_1_z[1]), .B(controlled_buffer_4_out), .A(controlled_buffer_11_out),
    .Z(alu15_1_z[0]), .OP(ALUOP), .O(alu15_1_z[3]));  // open: OIN, CIN, R
  // Probe on ALU
  // Probe on controlled_buffer_11_out
  // Probe on ALUFLAG
  Bit_Extender #(.in_width(4), .out_width(8), .\type ("input")) bit_extender_5 (
    .in(alu15_1_z), .out(ALUFLAG));  // open: extend
  or or_4 (or_4_out, multiplexer_4_out, IB[3]);
  // Probe on 4'b1100
  Register register_4 (.D(ALU[7:0]), .en(SRFW), .clk(CLK), .Q(SRF));  // open: clr
  and and_4 (jump, decoder_2_out3, or_4_out);
  assign not_9_out = ~multiplexer_5_out;  // NOT_Gate not_9, 4 bits wide
  Multiplexer #(.select(3), .width(4), .enable("false")) multiplexer_5 (
    .in0(4'b0000), .in1(4'b0000), .in2(4'b1100), .in3(4'b1100), .in4(4'b1100), .in5(4'b1000), .in6(4'b1000),
    .in7(4'b1000), .out(multiplexer_5_out), .sel(IB[2:0]));
  assign bit_extender_6_out = {{7{1'b0}}, SRF};  // Bit_Extender bit_extender_6
  assign bit_extender_7_out = {{7{1'b0}}, {F[7], I, E, F[4], O, C, N, Z}};  // Bit_Extender bit_extender_7
  Register #(.width(3)) register_5 (.D(IB[7:5]), .clk(KLC), .Q(register_5_q));  // open: en, clr
  // Probe on ALU
  // Probe on PC
  assign flagWm[3:0] = not_9_out & decode15_1_flagwm;  // AND_Gate and_5, 4 bits wide
  assign controlled_buffer_14_out = ALu_t ? ALU[7:0] : 8'bz;  // Controlled_Buffer controlled_buffer_14
  assign controlled_buffer_14_out = ALuf ? ALUFLAG : 8'bz;  // Controlled_Buffer controlled_buffer_15
  assign controlled_buffer_14_out = SRf_t ? SRF : 8'bz;  // Controlled_Buffer controlled_buffer_16
  not not_10 (not_10_out, load);
  assign controlled_buffer_17_out = tPC ? NPC : 15'bz;  // Controlled_Buffer controlled_buffer_17
  assign controlled_buffer_17_out = tF ? bit_extender_7_out : 15'bz;  // Controlled_Buffer controlled_buffer_18
  assign controlled_buffer_19_out = load ? DATA : 15'bz;  // Controlled_Buffer controlled_buffer_19
  assign controlled_buffer_20_out = load ? register_5_q : 3'bz;  // Controlled_Buffer controlled_buffer_20
  // Probe on adder15_1_s
  ADDER15 adder15_1 (.B(ALU), .A(PC), .S(adder15_1_s));  // open: COUT, CIN
  T_Flip_Flop t_ff_1 (.T(jump), .clk(KLC), .Q(t_ff_1_q), .reset(and_6_out));  // open: Qn, preset
  FLAGS8 flags8_1 (
    .F({F[7], I, E, F[4], O, C, N, Z}), .CLK(CLK), .WM(flagWm), .IRQ(IRQ), .NF(controlled_buffer_14_out));
  // Probe on flagWm
  assign controlled_buffer_19_out = not_10_out ? controlled_buffer_17_out : 15'bz;  // Controlled_Buffer controlled_buffer_21
  assign controlled_buffer_17_out = tALU ? ALU : 15'bz;  // Controlled_Buffer controlled_buffer_22
  assign controlled_buffer_17_out = tSRP ? SRP : 15'bz;  // Controlled_Buffer controlled_buffer_23
  assign controlled_buffer_17_out = tSRF ? bit_extender_6_out : 15'bz;  // Controlled_Buffer controlled_buffer_24
  assign controlled_buffer_20_out = not_10_out ? IB[7:5] : 3'bz;  // Controlled_Buffer controlled_buffer_25
  assign controlled_buffer_26_out = jump ? adder15_1_s : 15'bz;  // Controlled_Buffer controlled_buffer_26
  assign controlled_buffer_26_out = SWI ? {15{1'b1}} : 15'bz;  // Controlled_Buffer controlled_buffer_27
  T_Flip_Flop t_ff_2 (.T(t_ff_1_q), .clk(KLC), .Q(t_ff_2_q), .reset(and_6_out));  // open: Qn, preset
  or or_5 (or_5_out, load, regW);
  Counter #(.width(15), .max('h7fff)) counter_1 (
    .load(or_6_out), .up(1'b1), .count(and_7_out), .clk(CLK), .D(controlled_buffer_26_out),
    .carry(counter_1_carry), .Q(NPC));  // open: clr
  or or_6 (or_6_out, jump, SWI, sRP_t);
  assign controlled_buffer_26_out = sRP_t ? SRP : 15'bz;  // Controlled_Buffer controlled_buffer_28
  // Probe on IB[7:5]
  and and_6 (and_6_out, t_ff_2_q, t_ff_1_q);
  xor xor_1 (jumpin, t_ff_2_q, t_ff_1_q);
  and and_7 (and_7_out, not_11_out, count);
  // Probe on sr1
  REGS15 regs15_1 (
    .R4(R4), .A(sr1), .SelD(controlled_buffer_20_out), .R0(R0), .CLK(KLC), .B(sr2), .R5(R5), .R1(R1),
    .R3(R3), .R7(R7), .W(or_5_out), .SelB(IB[13:11]), .SelA(IB[10:8]), .D(controlled_buffer_19_out), .R6(R6),
    .R2(R2));
  // Probe on sr2
  not not_11 (not_11_out, counter_1_carry);
  Register #(.width(15)) register_6 (.D(NPC), .clk(CLK), .Q(register_6_q));  // open: en, clr
  Register #(.width(15)) register_7 (.D(register_6_q), .clk(CLK), .Q(PC));  // open: en, clr

  // Other names for the same wires on the sheet: ssr1[2:0] = IB[10:8]; ssr2[2:0] = IB[13:11]; SSign = IB[14];
  //   F (some bits) = {I, E, O, C, N, Z}; OP[3:0] = IB[3:0]; srd[2:0] = IB[7:5]; zero[14:0] = R0
endmodule
